# Fritzing sketch schema (saved by Fritzing 0.9.6b)
stripboards: 1

parts:
  Part1 = Arduino Uno (Rev3)
  LCD1 = LCD screen
  LED1 = LED - 5mm [color="Red (633nm)" current=0.030 package="5 mm [THT]"]
  Mod1 = Passive Buzzer
  KEYPAD1 = Membrane Matrix Keypad
  LCM1602_IIC1 = LCM1602 IIC [part_number="LCM1602 IIC" chip_label="LCM1602 IIC" package="DIP (Dual Inline) [THT]"]
  R1 = Resistor [tolerance=±5% power=0.25 resistance=220 package=THT]

nets:
  N1: Part1.A4/SDA, LCM1602_IIC1.SDA
  N2: Part1.A5/SCL, LCM1602_IIC1.SCL
  N3: Part1.D8, KEYPAD1.2
  N4: Part1.D9_PWM, Mod1.NC
  N5: Part1.D12/MISO, R1.Pin_0
  GND: Part1.GND, LED1.cathode, Mod1.-, LCM1602_IIC1.GND
  N6: Part1.D2, KEYPAD1.5
  N7: Part1.D3_PWM, KEYPAD1.1
  N8: Part1.D4, KEYPAD1.3
  N9: Part1.D5_PWM, KEYPAD1.4
  N10: Part1.D6_PWM, KEYPAD1.6
  N11: Part1.D7, KEYPAD1.7
  5V: Part1.5V, Mod1.S, LCM1602_IIC1.VCC
  VSS: LCD1.VSS, LCM1602_IIC1.VSS
  VDD: LCD1.VDD, LCM1602_IIC1.VDD
  N12: LCD1.V0, LCM1602_IIC1.V0
  N13: LCD1.RS, LCM1602_IIC1.RS
  N14: LCD1.R/W, LCM1602_IIC1.RW
  N15: LCD1.E, LCM1602_IIC1.E
  N16: LCD1.DB0, LCM1602_IIC1.D0
  N17: LCD1.DB1, LCM1602_IIC1.D1
  N18: LCD1.DB2, LCM1602_IIC1.D2
  N19: LCD1.DB3, LCM1602_IIC1.D3
  N20: LCD1.DB4, LCM1602_IIC1.D4
  N21: LCD1.DB5, LCM1602_IIC1.D5
  N22: LCD1.DB6, LCM1602_IIC1.D6
  N23: LCD1.DB7, LCM1602_IIC1.D7
  N24: LCD1.LED+, LCM1602_IIC1.A
  N25: LCD1.LED-, LCM1602_IIC1.K
  N26: LED1.anode, R1.Pin_1
  N27: LCM1602_IIC1.LED_A, LCM1602_IIC1.LED_B

custom parts:
  Membrane Matrix Keypad: Membrane Matrix 3x4 Keypad
  LCM1602 IIC: I2C-Module to use a 1602 or 2004 LCD on with the wire.h libory Serial LCD Modul
